# Fritzing sketch LED_schematic (saved by Fritzing 0.9.3b)
breadboards: 1

parts:
  LED1 = RGB LED (com. cathode, rgb) [package="5 mm [THT]"]
  Raspberry_Pi_1 = Raspberry Pi 3 [part_number=RPI-3-V1.2]
  R1 = Resistor [tolerance=±5% resistance=470 package=THT]
  R2 = Resistor [tolerance=±5% resistance=470 package=THT]
  R3 = Resistor [tolerance=±5% resistance=470 package=THT]

nets:
  N1: LED1.red_anode, R3.Pin_1
  N2: LED1.common_cathode, Raspberry_Pi_1.GND
  N3: LED1.green_anode, R2.Pin_1
  N4: LED1.blue_anode, R1.Pin_1
  N5: Raspberry_Pi_1.GPIO17, R3.Pin_0
  N6: Raspberry_Pi_1.GPIO27, R2.Pin_0
  N7: Raspberry_Pi_1.GPIO22, R1.Pin_0
